# Fritzing sketch Farm solenoid valve board (saved by Fritzing 0.9.3b)
breadboards: 1

parts:
  U1 = NodeMCU V1.0
  Part1 = Logic Level Converter
  U2 = 2-Channel 5v Relay Shield [package=relay-2ch5v10a]
  Part2 = Solar Cell
  Part3 = Solar Charge Controller [part_number="HGX Series Solar Charge Controller PWM" package=PWM-Model]
  BAT1 = LIPO-2000mAh [package=lipo-2000]
  U3 = LM2596 step down module
  U4 = 7-SEGMENT-4DIGIT [package=7-segment-4digit]
  S3 = SWITCH-MOMENTARY-2 [package=tactile-switch-1101ne]
  S4 = SWITCH-MOMENTARY-2 [package=tactile-switch-1101ne]
  L1 = Solenoid
  S5 = SWITCH-DPDT [package=gpi-152-3013]

nets:
  N1: U1.D1, Part1.TX_LV, S4.1
  N2: U1.D2, Part1.TX2_LV, S3.1
  N3: U1.3V3, Part1.LV
  GND: U1.GND, Part1.GND, U2.GND, U2.K1-Off, U2.K2-Off, Part3.Connector_6, U3.IN-, U3.OUT-, S3.2, S4.2, S5.4, S5.6
  VIN: U1.Vin, Part1.HV, U2.VCC, U3.OUT+, S5.3
  N4: Part1.TX_HV, U2.IN1
  N5: U2.K1-In, L1.pin2
  N6: U2.K1-On, U2.K2-On, Part3.Connector_5, U3.IN+, S5.1
  N7: U2.K2-In, L1.pin1
  N8: Part2.+, Part3.Connector_1
  N9: Part2.-, Part3.Connector_2
  N10: Part3.Connector_3, BAT1.+
  N11: Part3.Connector_4, BAT1.-
  N12: U4.3, S5.2
  N13: U4.4, S5.5

notes:
  12V 6ah SLA Battery
  https://www.jaycar.com.au/12v-6ah-sla-battery/p/SB2485
  LED to read voltages on either side of the regulator (battery/Solar on left and 5V on right)
  https://www.ebay.com.au/itm/Digital-Red-LED-Voltmeter-3V-30V-Car-Auto-Gauge-Voltage-Volt-Panel-Meter/233041877557?ssPageName=STRK%3AMEBIDX%3AIT&_trksid=p2057872.m2749.l2649
  ~12V down to 5V
  Relay board wired to switch polarity to latching solenoid
  https://www.ebay.com.au/itm/DC-5V-12V-1-2-4-8-Channel-Optocoupler-Relay-Module-Support-high-and-low-trigger/273802234110?ssPageName=STRK%3AMEBIDX%3AIT&var=573489108310&_trksid=p2057872.m2749.l2649
  2 x momentary push buttons as a local/manual way to activate Relays and open/close solenoid valve
  https://www.jaycar.com.au/black-momentary-ip65-pushbutton-switch/p/SP0756
  12v DC Latching Irrigation Solenoid Valve
  https://www.hillsirrigation.com.au/HUNTER-DC-LATCHING-COIL-SUITS-PGV-SOLENOID-VALVES
  Centre-off sprung DPDT switch.
  https://www.jaycar.com.au/dpdt-switch-centre-off-spring-return-both-sides/p/SK0980

custom parts:
  NodeMCU V1.0: ESP8266 based NodeMCU
  2-Channel 5v Relay Shield: 2 Channel 5v Relay Shield w. 2x SPD-06VDC-SD-C
  Solar Charge Controller: PWM-Solar Charge Controller
  LM2596 step down module: LM2596 DC-DC step down power supply module 3 A.
